# Fritzing sketch doorbell-circuit (saved by Fritzing 0.3.19b)

parts:
  Arduino1 = Arduino
  R1 = Resistor [resistance=220 package=THT]
  J1 = Basic Servo
  U1 = mystery part, 3 pins [chip_label=Doorbell spacing=300mil]

nets:
  GND: Arduino1.GND, J1.gnd, U1.pin1
  N1: Arduino1.D9, J1.pulse
  N2: Arduino1.3V3, U1.pin2
  +5V: Arduino1.+5V, J1.vcc
  N3: Arduino1.A5, R1.Pin_0
  N4: R1.Pin_1, U1.pin3
